// Logisim project Project_1.circ as structural Verilog: 1 circuit, main circuit main
module main (
  input  in_1,
  input  in_2,
  input  in_3,
  output out_4
);

  wire nand_1_out, nand_3_out, nand_4_out, not_1_out;

  not not_1 (not_1_out, in_1);
  not not_2 (not_1_out, in_1);
  not not_3 (not_1_out, in_1);
  not nand_1 (nand_1_out, in_1);  // NAND_Gate
  nand nand_2 (nand_1_out, in_1, in_1);
  not nand_3 (nand_3_out, not_1_out);  // NAND_Gate
  not nand_4 (nand_4_out, not_1_out);  // NAND_Gate
  not nand_5 (nand_4_out, not_1_out);  // NAND_Gate
  nand nand_6 (out_4, nand_1_out, nand_1_out, nand_3_out, nand_4_out, nand_4_out);

  assign in_2 = in_1;
  assign in_3 = in_1;

  // Notes on the sheet:
  //   A
  //   B
  //   C
  //   ABC
  //   A'BC
  //   AB'C'
  //   AB'C
  //   A'B'C
  //   C+AB'
endmodule
