// Logisim project Project_1_AND_OR.circ as structural Verilog: 1 circuit, main circuit main
module main (
  input  in_1,
  input  in_2,
  input  in_3,
  output out_4
);

  wire and_1_out, and_3_out, and_4_out, not_1_out;

  not not_1 (not_1_out, in_1);
  not not_2 (not_1_out, in_1);
  not not_3 (not_1_out, in_1);
  and and_1 (and_1_out, in_1, in_1, in_1);
  and and_2 (and_1_out, not_1_out, in_1);
  and and_3 (and_3_out, in_1, not_1_out, not_1_out);
  and and_4 (and_4_out, in_1, not_1_out, in_1);
  and and_5 (and_4_out, not_1_out, not_1_out, in_1);
  or or_1 (out_4, and_1_out, and_1_out, and_3_out, and_4_out, and_4_out);

  assign in_2 = in_1;
  assign in_3 = in_1;

  // Notes on the sheet:
  //   A
  //   B
  //   C
  //   ABC
  //   A'BC
  //   AB'C'
  //   AB'C
  //   A'B'C
  //   C+AB'
endmodule
